# Fritzing sketch Schematic (saved by Fritzing 0.9.3b)
perfboards: 1

parts:
  part = 28BYJ-48 Stepper Motor [part_number=28BYJ-48]  # not connected
  part_2 = 28BYJ-48 Driver Module [part_number=ULN2003 package=THT]
  PCF8575 = PFC8575 module
  Hall_Effect_Not = Hall Sensor [part_number=WSH130 package=TO92]
  4_Pin_JST_To_Next_Module = Header 4 [package=1x04-1mm-ra]
  4_Pin_JST_To_Prev_Module = Header 4 [package=1x04-1mm-ra]

nets:
  N1: part_2.IN1, PCF8575.Pin_7
  N2: part_2.IN2, PCF8575.Pin_6
  N3: part_2.IN3, PCF8575.Pin_5
  N4: part_2.IN4, PCF8575.Pin_4
  N5: PCF8575.Pin_1, PCF8575.Pin_20, Hall_Effect_Not.GND
  N6: PCF8575.Pin_2, PCF8575.Pin_19, Hall_Effect_Not.VCC
  N7: PCF8575.Pin_18, Hall_Effect_Not.OUT
  N8: PCF8575.Pin_23, 4_Pin_JST_To_Next_Module.4, 4_Pin_JST_To_Prev_Module.4
  N9: PCF8575.Pin_24, 4_Pin_JST_To_Next_Module.3, 4_Pin_JST_To_Prev_Module.3
  N10: 4_Pin_JST_To_Next_Module.1, 4_Pin_JST_To_Prev_Module.1

notes:
  Regular Module

custom parts:
  28BYJ-48 Stepper Motor: Unipolar Stepper Motor 28BYJ-48 Top coil - pink & orange Bottom coil - blue & yellow Common rail - red Connector pins: blue - pink - yellow - orange - red
  28BYJ-48 Driver Module: Generic male header
  PFC8575 module: PCF8575 IO Expander Module I2C To 16IO.
  Hall Sensor: A Hall Sensor
